# Fritzing sketch EMDR V2 (saved by Fritzing 0.9.3b)
circuit board: 8.60583cm x 6.22578cm
breadboards: 1

parts:
  LLC1 = Logic Level Converter [package="Breakout board"]
  R1 = Rotary Potentiometer (Large) [maximum_resistance=100kΩ package=THT]
  F2 = Resettable Fuse PTC [package=ptc]
  S1 = SWITCH-MOMENTARY-2 [package=tactile_switch_tall]
  J1 = Power Jack [package=power_jack_slot]
  J2 = screw terminal, 3 pins
  J4 = screw terminal, 2 pins
  C1 = Electrolytic Capacitor [capacitance=1mF voltage=63V package="300 mil [THT, electrolytic]"]
  WeMos_D1_Mini2 = WeMos D1 Mini
  R1_2 = Resistor [tolerance=±5% resistance=68 package=THT]
  WeMos_D1_Mini1 = WeMos D1 Mini
  J3 = female pin header, 4 pins [form="♀ (female)"]
  R2 = Resistor [tolerance=±5% resistance=4.7k package=THT]
  R3 = Resistor [tolerance=±5% resistance=4.7k package=THT]
  SW1 = DIP SWITCH [package=dipswitch-02]
  R4 = Resistor [tolerance=±5% resistance=10k package=THT]
  R5 = Resistor [tolerance=±5% resistance=10k package=THT]
  Pad1 = Pad [width=5 height=5 connect=center]
  Pad2 = Pad [width=5 height=5 connect=center]
  Pad3 = Pad [width=3 height=3 connect=center]
  F1 = Resettable Fuse PTC [package=ptc]

nets:
  N1: LLC1.LV1, WeMos_D1_Mini1.D4
  N2: LLC1.LV, R1.leg1, WeMos_D1_Mini1.3V3, J3.pin2, R2.Pin_0, R3.Pin_0, R4.Pin_0, R5.Pin_0, Pad3.pad
  N3: LLC1.L-GND, LLC1.H-GND, R1.leg2, S1.2, J1.GNDBREAK, J1.GND, J2.pin3, C1.-, WeMos_D1_Mini2.G, WeMos_D1_Mini1.G, J3.pin1, SW1.1, SW1.2, Pad2.pad
  5V: LLC1.HV, F2.1, WeMos_D1_Mini2.5V, WeMos_D1_Mini1.5V
  N4: LLC1.HV1, R1_2.Pin_0
  N5: R1.wiper, WeMos_D1_Mini1.A0
  N6: F2.2, J1.PWR, F1.2
  N7: S1.1, WeMos_D1_Mini1.D3
  N8: J2.pin1, J4.pin1, Pad1.pad
  N9: J2.pin2, R1_2.Pin_1
  N10: J4.pin2, C1.+, F1.1
  N11: WeMos_D1_Mini2.D1, WeMos_D1_Mini1.D8
  N12: WeMos_D1_Mini1.D1, J3.pin3, R3.Pin_1
  N13: WeMos_D1_Mini1.D2, J3.pin4, R2.Pin_1
  N14: WeMos_D1_Mini1.D6, SW1.4, R4.Pin_1
  N15: WeMos_D1_Mini1.D7, SW1.3, R5.Pin_1

notes:
  Gnd
  5v
  3v
  Speed
  SDA
  COM
  SCL
  NO

custom parts:
  Logic Level Converter: 5V to/from 3.3V logic level converter
